# Fritzing sketch Arduino Uno mit MCP4725 (saved by Fritzing 0.9.3b)
breadboards: 1

parts:
  Bauteil1 = Adafruit MCP4725 Breakout Board - 12-Bit DAC [part_number="Adafruit #935"]
  Bauteil2 = Arduino Uno (Rev3)

nets:
  GND: Bauteil1.GND, Bauteil2.GND
  N1: Bauteil1.SCL, Bauteil2.A5/SCL
  N2: Bauteil1.SDA, Bauteil2.A4/SDA
  N3: Bauteil1.VOUT, Bauteil2.A0

custom parts:
  Adafruit MCP4725 Breakout Board - 12-Bit DAC: Your microcontroller probably has an ADC (analog -> digital converter) but does it have a DAC (digital -> analog converter)??? Now it can! This breakout board features the easy-to-use MCP4725 12-bit DAC. Control it via I2C and send it the value you want it to output, and the VOUT pin will have it. Great for audio / analog projects, such as when you can't use PWM but need a sine wave or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
